// Logisim project componente_04.circ as structural Verilog: 1 circuit, main circuit main
module main (
  input  [7:0] C1,
  output [7:0] Y
);

  Adder adder_1 (.a(C1), .b(8'h4), .out(Y));  // open: cin, cout
endmodule
