// Logisim project componente_06.circ as structural Verilog: 1 circuit, main circuit main
module main (
  input  [2:0] A1,
  input  in_2,
  input  in_3,
  input  in_4,
  output y
);

  wire clock_1_out;

  Clock clock_1 (.out(clock_1_out));
  RAM #(.addrWidth(3), .dataWidth(1)) ram_1 (.addr(A1), .data(y), .sel(in_2), .clk(clock_1_out), .ld(in_3), .clr(in_4));
endmodule
