// Logisim project componente_10.circ as structural Verilog: 1 circuit, main circuit main
module main (
  input  [7:0] A,
  input  in_2,
  input  in_3,
  input  [3:0] in_4,
  input  [7:0] B,
  input  [2:0] in_6,
  output [7:0] out_7
);

  wire [7:0] _0000_out, _0001_out, _0010_out, _0011_out, _0100_out, _0101_out, adder_1_out, shifter_1_out,
       shifter_2_out, subtractor_1_out;

  assign _0000_out = A & B;  // AND_Gate _0000, 8 bits wide
  assign _0001_out = A | B;  // OR_Gate _0001, 8 bits wide
  assign _0010_out = ~A;  // NOT_Gate _0010, 8 bits wide
  Adder adder_1 (.a(A), .out(adder_1_out), .cout(in_2));  // open: b, cin
  Subtractor subtractor_1 (.a(A), .b(B), .out(subtractor_1_out), .bout(in_3));  // open: bin
  Shifter shifter_1 (.in(A), .\dist (in_6), .out(shifter_1_out));
  Shifter #(.shift("lr")) shifter_2 (.in(A), .\dist (in_6), .out(shifter_2_out));
  assign _0011_out = ~(A & B);  // NAND_Gate _0011, 8 bits wide
  assign _0100_out = ~(A | B);  // NOR_Gate _0100, 8 bits wide
  assign _0101_out = A ^ B;  // XOR_Gate _0101, 8 bits wide
  Multiplexer #(.select(4), .width(8)) multiplexer_1 (
    .in0(_0000_out), .in1(_0001_out), .in2(_0010_out), .in3(_0011_out), .in4(_0100_out), .in5(_0101_out),
    .in6(adder_1_out), .in7(subtractor_1_out), .in8(shifter_1_out), .in9(shifter_2_out), .in10({8{1'b0}}),
    .in11({8{1'b0}}), .in12({8{1'b0}}), .in13({8{1'b0}}), .in14({8{1'b0}}), .in15({8{1'b0}}), .out(out_7),
    .sel(in_4));  // open: en

  // Notes on the sheet:
  //   0110
  //   0111
  //   1000
  //   1001
endmodule
